# Fritzing sketch oregon (saved by Fritzing 0.9.3b)
circuit board: 8.46667cm x 5.64444cm
breadboards: 1

parts:
  Composant1 = Arduino Nano (Rev3.0)
  U1 = RXB6 Superhetrodyne receiver [part_number=RXB6 package=sip]

nets:
  N1: Composant1.GND, U1.DGND
  N2: Composant1.D2, U1.DATA
  N3: Composant1.5V, U1.DVCC

notes:
  173 mm wire (antenna)

custom parts:
  RXB6 Superhetrodyne receiver: RF Link receivers RXB6, 315, 433.92 Mhz (or custom) Converted from the Spartfun Rf-LINK_RX part (which doesn't apper to be quite correct).
